# Fritzing sketch Spectrometer Wiring Diagram (saved by Fritzing 0.9.3b)
breadboards: 1

parts:
  R1 = Resistor [tolerance=±5% resistance=220 package=THT]
  R2 = Resistor [tolerance=±5% resistance=220 package=THT]
  Part1 = Arduino Uno (Rev3)
  LED1 = LED - 5mm [color="White (4500K)" package="5 mm [THT]"]
  LED2 = LED - 5mm [color="White (4500K)" package="5 mm [THT]"]
  Part2 = Adafruit AS7262 Visible Spetral Sensor [part_number="Adafruit #3779"]

nets:
  N1: R1.Pin_1, R2.Pin_1, Part1.5V
  N2: Part1.A4/SDA, Part2.TX/SDA
  N3: Part1.A5/SCL, Part2.RX/SCL
  GND: Part1.GND, LED1.cathode, LED2.cathode, Part2.GND
  3V3: Part1.3V3, Part2.VIN
